# Fritzing sketch project_plan (saved by Fritzing 0.9.3b)
breadboards: 1

parts:
  Mod1 = Raspberry Pi 4B
  J1 = Basic Servo
  Part1 = Logic Level Converter
  Part2 = Adafruit VL530X Time of Flight Distance Sensor [part_number="Adafruit #3317"]
  R1 = Resistor [tolerance=±5% resistance=220 package="0603 [SMD]"]
  R2 = Resistor [tolerance=±5% resistance=220 package="0603 [SMD]"]
  R3 = Resistor [tolerance=±5% resistance=220 package="0603 [SMD]"]

nets:
  3V3: Mod1.3V3, Part1.LV, Part2.VCC, R1.Pin_1, R2.Pin_1, R3.Pin_1
  N1: Mod1.GPIO2, Part2.SDA, R2.Pin_0
  5V: Mod1.5V, J1.vcc, Part1.HV
  N2: Mod1.GPIO3, Part2.SCL, R3.Pin_0
  GND: Mod1.GND, J1.gnd, Part1.GND, Part2.GND
  N3: Mod1.GPIO18, Part1.TX_LV
  N4: J1.pulse, Part1.TX_HV
  N5: Part2.XSHUT, R1.Pin_0

custom parts:
  Adafruit VL530X Time of Flight Distance Sensor: The VL53L0X is a Time of Flight distance sensor like no other you've used! The sensor contains a very tiny invisible laser source, and a matching sensor. The VL53L0X can detect the "time of flight", or how long the light has taken to bounce back to the sensor. Since it uses a very narrow light source, it is good for determining distance of only the surface directly in front of it. Unlike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
